# Fritzing sketch roulette (saved by Fritzing 0.9.3b)
breadboards: 1

parts:
  Part1 = Arduino Uno (Rev3) - ICSP
  S1 = Pushbutton [package="[SMD]"]
  S2 = Pushbutton [package="[SMD]"]
  S3 = Pushbutton [package="[SMD]"]
  R1 = Resistor [tolerance=±5% resistance=220 package="0402 [SMD]"]
  R2 = Resistor [tolerance=±5% resistance=220 package="0402 [SMD]"]
  R3 = Resistor [tolerance=±5% resistance=220 package="0402 [SMD]"]
  Part2 = 24 NeoPixel Ring [part_number=1586]

nets:
  5V: Part1.5V, Part2.VDD
  N1: Part1.D9_PWM, S1.Pin_1, S1.Pin_2, R3.Pin_0
  N2: Part1.D11_PWM/MOSI, S3.Pin_1, S3.Pin_2
  N3: Part1.D7, Part2.IN
  N4: Part1.3V3, S1.Pin_3, S1.Pin_4, S2.Pin_3, S2.Pin_4, S3.Pin_3, S3.Pin_4
  N5: Part1.GND, Part2.OUT
  N6: S2.Pin_1, S2.Pin_2, R2.Pin_0
  N7: R1.Pin_1, R2.Pin_1, R3.Pin_1

custom parts:
  24 NeoPixel Ring: 24 ultra bright smart LED NeoPixels are arranged in a circle with 2.6" (66mm) outer diameter. The rings are 'chainable' - connect the output pin of one to the input pin of another. Use only one microcontroller pin to control as many as you can chain together! Each LED is addressable as the driver chip is inside the LED. Each one has ~18mA constant current drive so the color will be very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
